# Fritzing sketch Air_Quality_Adv (saved by Fritzing 0.9.10b)
breadboards: 1

parts:
  Raspberry_Pi_4_Model_B = Raspberry Pi 4B
  MQ-7 = GAS_SENSOR [package=mq-3]
  MQ-135 = GAS_SENSOR [package=mq-3]
  MQ-2 = GAS_SENSOR [package=mq-3]
  ADC1 = MCP3008 [package=dil16]
  part = Sharp Dust Sensor [part_number=GP2Y1010AU0F]
  KY-026 = KY-026 Flame Sensor Module [package="Breakout board"]
  DHT22 = DHT22 Humidity and Temperature Sensor
  MQ-4 = GAS_SENSOR [package=mq-3]
  Buzzer = Piezo Speaker
  Part1 = Logic Level Converter
  LCM1602_I2C = LCM1602 IIC [part_number="LCM1602 IIC" chip_label="LCM1602 IIC" package="DIP (Dual Inline) [THT]"]
  LCD_2004_I2C = 20x4 LCD display [part_number=2004A]
  Relay_1_Channel = KY-019 5V Relay Module [package="Breakout board"]
  Relay_1_Channel_2 = KY-019 5V Relay Module [package="Breakout board"]

nets:
  VDD: Raspberry_Pi_4_Model_B.3V3, ADC1.VREF, ADC1.VDD, KY-026.+, DHT22.VDD, Part1.LV
  N1: Raspberry_Pi_4_Model_B.GPIO2, LCM1602_I2C.SDA
  VCC: Raspberry_Pi_4_Model_B.5V, MQ-7.B1, MQ-135.B1, MQ-2.B1, part.V-LED, part.VCC, MQ-4.B1, Part1.HV, LCM1602_I2C.VCC, Relay_1_Channel.+, Relay_1_Channel_2.+
  N2: Raspberry_Pi_4_Model_B.GPIO3, LCM1602_I2C.SCL
  GND: Raspberry_Pi_4_Model_B.GND, MQ-7.A1, MQ-135.A1, MQ-2.A1, ADC1.DGND, ADC1.AGND, part.LED-GND, part.S-GND, KY-026.G, DHT22.GND, MQ-4.A1, Buzzer.pin1, Part1.GND, LCM1602_I2C.GND, Relay_1_Channel.-, Relay_1_Channel_2.-
  N3: Raspberry_Pi_4_Model_B.GPIO17, Relay_1_Channel_2.S
  N4: Raspberry_Pi_4_Model_B.GPIO27, Relay_1_Channel.S
  N5: Raspberry_Pi_4_Model_B.GPIO23, part.LED
  N6: Raspberry_Pi_4_Model_B.GPIO10, ADC1.Din
  N7: Raspberry_Pi_4_Model_B.GPIO9, ADC1.Dout
  N8: Raspberry_Pi_4_Model_B.GPIO11, ADC1.CLK
  N9: Raspberry_Pi_4_Model_B.GPIO8, ADC1.CS/SHDN
  N10: Raspberry_Pi_4_Model_B.GPIO19, Buzzer.pin2
  N11: Raspberry_Pi_4_Model_B.GPIO26, DHT22.DATA
  N12: Raspberry_Pi_4_Model_B.GPIO21, KY-026.D0
  N13: MQ-7.H2, Part1.RX2_HV
  N14: MQ-135.H2, MQ-2.H2, Part1.TX2_HV
  N15: ADC1.CH1, ADC1.CH2, Part1.TX2_LV
  N16: ADC1.CH3, Part1.RX2_LV
  N17: ADC1.CH4, ADC1.CH5, Part1.TX_LV
  N18: part.Vo, MQ-4.H2, Part1.TX_HV
  VSS: LCM1602_I2C.VSS, LCD_2004_I2C.Vss
  VDD_2: LCM1602_I2C.VDD, LCD_2004_I2C.Vdd
  N19: LCM1602_I2C.V0, LCD_2004_I2C.Vo
  N20: LCM1602_I2C.RS, LCD_2004_I2C.RS
  N21: LCM1602_I2C.RW, LCD_2004_I2C.R/W
  N22: LCM1602_I2C.E, LCD_2004_I2C.E
  N23: LCM1602_I2C.D0, LCD_2004_I2C.DB0
  N24: LCM1602_I2C.D1, LCD_2004_I2C.DB1
  N25: LCM1602_I2C.D2, LCD_2004_I2C.DB2
  N26: LCM1602_I2C.D3, LCD_2004_I2C.DB3
  N27: LCM1602_I2C.D4, LCD_2004_I2C.DB4
  N28: LCM1602_I2C.D5, LCD_2004_I2C.DB5
  N29: LCM1602_I2C.D6, LCD_2004_I2C.DB6
  N30: LCM1602_I2C.D7, LCD_2004_I2C.DB7
  N31: LCM1602_I2C.A, LCD_2004_I2C.A_+
  N32: LCM1602_I2C.K, LCD_2004_I2C.K_-

notes:
  3.3V
  5V

custom parts:
  Sharp Dust Sensor: Sharp GP2Y1010AU0F Dust Sensor
  KY-026 Flame Sensor Module: KY-026 Flame Sensor Module reacts in the presence of fire.
  LCM1602 IIC: I2C-Module to use a 1602 or 2004 LCD on with the wire.h libory Serial LCD Modul
  20x4 LCD display: 20x4 character display. CHECK LED POLARITY BEFORE CONNECTING POWER Some versions of the dispaly have the polarity of the LED pins "A" and "K" reversed.
  KY-019 5V Relay Module: KY-019 5V Relay module, used to control AC circuits. (Special thanks to vanepp for fixing the PCB holes and other errors)
